// Logisim project cpu.circ as structural Verilog: 5 circuits, main circuit main
module main (
  input  [4:0] in_1,
  input  [3:0] in_2,
  input  [1:0] in_3,
  input  [1:0] in_4,
  output [15:0] out_5,
  output [15:0] out_6
);

  wire clock_1_out;
  wire [1:0] decoder_1_out0, decoder_2_out0;
  wire [2:2] decoder_1_out2, decoder_2_out2;
  wire [3:3] decoder_1_out3, decoder_2_out3;
  wire [15:0] controlled_buffer_1_out, controlled_buffer_2_out, flags_q, pc_q, r0_q, r1_q, r2_q, r3_q;

  Register #(.width(16)) r0 (.Q(r0_q));  // open: D, en, clk, clr
  Register #(.width(16)) r1 (.Q(r1_q));  // open: D, en, clk, clr
  Register #(.width(16)) r2 (.Q(r2_q));  // open: D, en, clk, clr
  Register #(.width(16)) r3 (.Q(r3_q));  // open: D, en, clk, clr
  Decoder #(.select(2)) decoder_1 (
    .out0(decoder_1_out0[0]), .out1(decoder_1_out0[1]), .out2(decoder_1_out2[2]), .out3(decoder_1_out3[3]),
    .sel(in_3));  // open: en
  Decoder #(.select(2)) decoder_2 (
    .out0(decoder_2_out0[0]), .out1(decoder_2_out0[1]), .out2(decoder_2_out2[2]), .out3(decoder_2_out3[3]),
    .sel(in_4));  // open: en
  Register #(.width(16)) lr ();  // open: D, en, clk, Q, clr
  Register #(.width(16)) sp ();  // open: D, en, clk, Q, clr
  Register #(.width(16)) pc (.Q(pc_q));  // open: D, en, clk, clr
  assign controlled_buffer_1_out = decoder_1_out0[0] ? r0_q : 16'bz;  // Controlled_Buffer controlled_buffer_1
  assign controlled_buffer_2_out = decoder_2_out0[0] ? r0_q : 16'bz;  // Controlled_Buffer controlled_buffer_2
  assign controlled_buffer_1_out = decoder_1_out0[1] ? r1_q : 16'bz;  // Controlled_Buffer controlled_buffer_3
  assign controlled_buffer_2_out = decoder_2_out0[1] ? r1_q : 16'bz;  // Controlled_Buffer controlled_buffer_4
  assign controlled_buffer_1_out = decoder_1_out2[2] ? r2_q : 16'bz;  // Controlled_Buffer controlled_buffer_5
  assign controlled_buffer_2_out = decoder_2_out2[2] ? r2_q : 16'bz;  // Controlled_Buffer controlled_buffer_6
  assign controlled_buffer_1_out = decoder_1_out3[3] ? r3_q : 16'bz;  // Controlled_Buffer controlled_buffer_7
  assign controlled_buffer_2_out = decoder_2_out3[3] ? r3_q : 16'bz;  // Controlled_Buffer controlled_buffer_8
  Adder #(.width(16)) adder_1 (.a(pc_q), .b(16'h1));  // open: out, cin, cout
  Clock clock_1 (.out(clock_1_out));
  Register #(.width(16)) flags (.D(out_5), .en(1'b1), .clk(clock_1_out), .Q(flags_q));  // open: clr
  alu alu_1 (
    .A(controlled_buffer_1_out), .B(controlled_buffer_2_out), .Cond(in_2), .F(flags_q), .S(in_1), .Q(out_6),
    .FQ(out_5));
endmodule

module logicUnit (
  input  [15:0] A,
  input  [15:0] B,
  input  [2:0] S,
  output [15:0] Q
);

  wire [15:0] and_1_out, bit_extender_1_out, multiplexer_1_out, or_1_out, xor_1_out;

  assign bit_extender_1_out = {{15{S[2]}}, S[2]};  // Bit_Extender bit_extender_1
  assign and_1_out = A & B;  // AND_Gate and_1, 16 bits wide
  assign or_1_out = A | B;  // OR_Gate or_1, 16 bits wide
  Hex_Digit_Display hex_digit_display_1 (.value({1'b0, S}));  // open: dp
  assign xor_1_out = A ^ B;  // XOR_Gate xor_1, 16 bits wide
  Multiplexer #(.select(2), .width(16)) multiplexer_1 (
    .in0(and_1_out), .in1(or_1_out), .in2(xor_1_out), .in3(A), .out(multiplexer_1_out), .sel(S[1:0]));
  assign Q = multiplexer_1_out ^ bit_extender_1_out;  // XOR_Gate xor_2, 16 bits wide

  // Notes on the sheet:
  //   logic unit
  //   toggleable not
endmodule

module arithmaticUnit (
  input  [15:0] A,
  input  [15:0] B,
  input  [2:0] S,
  output [15:0] Q
);

  wire [15:0] adder_1_out, adder_2_out, multiplier_1_out, subtractor_1_out, subtractor_2_out;

  Hex_Digit_Display hex_digit_display_1 (.value({1'b0, S}));  // open: dp
  Adder #(.width(16)) adder_1 (.a(A), .b(B), .out(adder_1_out));  // open: cin, cout
  Subtractor #(.width(16)) subtractor_1 (.a(A), .b(B), .out(subtractor_1_out));  // open: bin, bout
  Adder #(.width(16)) adder_2 (.a(A), .b(16'h1), .out(adder_2_out));  // open: cin, cout
  Subtractor #(.width(16)) subtractor_2 (.a(A), .b(16'h1), .out(subtractor_2_out));  // open: bin, bout
  Multiplier #(.width(16)) multiplier_1 (.a(A), .b(B), .out(multiplier_1_out));  // open: cin, cout
  Multiplexer #(.select(3), .width(16)) multiplexer_1 (
    .in0(adder_1_out), .in1(subtractor_1_out), .in2(adder_2_out), .in3(subtractor_2_out),
    .in4(multiplier_1_out), .out(Q), .sel(S));  // open: in5, in6, in7

  // Notes on the sheet:
  //   a+b  a-b  a+1 a-1, a*b ?
endmodule

module alu (
  input  [15:0] A,
  input  [15:0] B,
  input  [4:0] S,
  input  [3:0] Cond,
  input  [15:0] F,
  output [15:0] Q,
  output [15:0] FQ
);

  wire and_1_out, and_2_out, and_4_out, demultiplexer_1_out0, demultiplexer_1_out1, demultiplexer_1_out2,
       demultiplexer_1_out3, not_1_out, not_2_out, or_1_out, or_2_out;
  wire [1:0] and_3_out, bit_extender_1_out;
  wire [15:0] arithmaticunit_1_q, flagupdater_1_q, logicunit_1_q;

  Demultiplexer #(.select(2)) demultiplexer_1 (
    .out0(demultiplexer_1_out0), .out1(demultiplexer_1_out1), .out2(demultiplexer_1_out2),
    .out3(demultiplexer_1_out3), .in(1'b1), .sel(S[4:3]));
  LED led_1 (.in(demultiplexer_1_out0));
  LED led_2 (.in(demultiplexer_1_out1));
  LED led_3 (.in(demultiplexer_1_out2));
  LED led_4 (.in(demultiplexer_1_out3));
  not not_1 (not_1_out, Cond[2]);
  and and_1 (and_1_out, Cond[2], F[14]);
  not not_2 (not_2_out, Cond[1]);
  and and_2 (and_2_out, Cond[1], F[15]);
  logicUnit logicunit_1 (.S(S[2:0]), .A(A), .B(B), .Q(logicunit_1_q));
  arithmaticUnit arithmaticunit_1 (.S(S[2:0]), .A(A), .B(B), .Q(arithmaticunit_1_q));
  or or_1 (or_1_out, not_1_out, and_1_out);
  or or_2 (or_2_out, not_2_out, and_2_out);
  Multiplexer #(.select(2), .width(16)) multiplexer_1 (
    .in0(A), .in1(B), .in2(logicunit_1_q), .in3(arithmaticunit_1_q), .out(Q), .sel(and_3_out));
  assign and_3_out = S[4:3] & bit_extender_1_out;  // AND_Gate and_3, 2 bits wide
  flagUpdater flagupdater_1 (.Res(Q), .Q(flagupdater_1_q));
  and and_4 (and_4_out, or_1_out, or_2_out);
  Multiplexer #(.width(16)) multiplexer_2 (.in0(F), .in1(flagupdater_1_q), .out(FQ), .sel(Cond[0]));
  assign bit_extender_1_out = {{1{and_4_out}}, and_4_out};  // Bit_Extender bit_extender_1

  // Notes on the sheet:
  //   neg flag conditional
  //   zero flag conditional
  //   if low pass A
endmodule

module flagUpdater (
  input  [15:0] Res,
  output [15:0] Q
);

  Comparator #(.width(16)) comparator_1 (.a(Res), .b({16{1'b0}}), .eq(Q[15]), .lt(Q[14]));  // open: gt

  assign Q[13:0] = {14{1'b0}};
endmodule
